# Fritzing sketch Bekant (saved by Fritzing 0.9.3b)
breadboards: 1

parts:
  Part1 = Arduino Uno (Rev3)
  U1 = MCP2003B [part_number=MCP2003B chip_label=U1 package=8-SOIC]
  R1 = Resistor [tolerance=±5% resistance=2.2k package=THT]
  R2 = Resistor [tolerance=±5% resistance=2.2k package=THT]
  R3 = Resistor [tolerance=±5% resistance=2.2k package=THT]
  R4 = Resistor [tolerance=±5% resistance=1k package=THT]

nets:
  N1: Part1.D0/RX, U1.RxD, R1.Pin_0
  N2: Part1.D1/TX, U1.TxD
  N3: Part1.5V, R1.Pin_1, R2.Pin_1
  GND/LIN Ground: Part1.GND, U1.Vss, R3.Pin_1
  12V: Part1.VIN, U1.Vbb, R4.Pin_1
  N4: U1.CS, R2.Pin_0
  N5: U1.!WAKE, R3.Pin_0
  LIN bus: U1.Lbus, R4.Pin_0

notes:
  LIN Bus
  LIN Ground
  12V Supply

custom parts:
  MCP2003B: LIN Transciever
